# Fritzing sketch 8x8amp (saved by Fritzing 0.9.3b)
circuit board: 10cm x 15cm
breadboards: 1

parts:
  Part1 = Arduino Uno (Rev3)
  R1 = Resistor [tolerance=±5% resistance=220 package=THT]
  Q8 = pnp-Powertransistor [package="TO220 [THT]"]
  Q9 = PNP-Transistor [package="TO92 [THT]"]
  R2 = Resistor [tolerance=±5% resistance=220 package=THT]
  Power_plug4 = Power plug
  R3 = Resistor [tolerance=±5% resistance=220 package=THT]
  R4 = Resistor [tolerance=±5% resistance=220 package=THT]
  Q10 = pnp-Powertransistor [package="TO220 [THT]"]
  Q11 = PNP-Transistor [package="TO92 [THT]"]
  R5 = Resistor [tolerance=±5% resistance=220 package=THT]
  R6 = Resistor [tolerance=±5% resistance=220 package=THT]
  Q12 = pnp-Powertransistor [package="TO220 [THT]"]
  Q13 = PNP-Transistor [package="TO92 [THT]"]
  R7 = Resistor [tolerance=±5% resistance=220 package=THT]
  R8 = Resistor [tolerance=±5% resistance=220 package=THT]
  Q14 = pnp-Powertransistor [package="TO220 [THT]"]
  Q15 = PNP-Transistor [package="TO92 [THT]"]
  R9 = Resistor [tolerance=±5% resistance=220 package=THT]
  R10 = Resistor [tolerance=±5% resistance=220 package=THT]
  Q16 = pnp-Powertransistor [package="TO220 [THT]"]
  Q17 = PNP-Transistor [package="TO92 [THT]"]
  R11 = Resistor [tolerance=±5% resistance=220 package=THT]
  R12 = Resistor [tolerance=±5% resistance=220 package=THT]
  Q18 = pnp-Powertransistor [package="TO220 [THT]"]
  Q19 = PNP-Transistor [package="TO92 [THT]"]
  R13 = Resistor [tolerance=±5% resistance=220 package=THT]
  R14 = Resistor [tolerance=±5% resistance=220 package=THT]
  Q20 = pnp-Powertransistor [package="TO220 [THT]"]
  Q21 = PNP-Transistor [package="TO92 [THT]"]
  R15 = Resistor [tolerance=±5% resistance=220 package=THT]
  R16 = Resistor [tolerance=±5% resistance=220 package=THT]
  Q22 = pnp-Powertransistor [package="TO220 [THT]"]
  Q23 = PNP-Transistor [package="TO92 [THT]"]
  Q24 = pnp-Powertransistor [package="TO220 [THT]"]
  Q25 = pnp-Powertransistor [package="TO220 [THT]"]
  Q26 = pnp-Powertransistor [package="TO220 [THT]"]
  Q27 = pnp-Powertransistor [package="TO220 [THT]"]
  Q28 = pnp-Powertransistor [package="TO220 [THT]"]
  Q29 = pnp-Powertransistor [package="TO220 [THT]"]
  Q31 = pnp-Powertransistor [package="TO220 [THT]"]
  R17 = Resistor [tolerance=±5% resistance=220 package=THT]
  R18 = Resistor [tolerance=±5% resistance=220 package=THT]
  R19 = Resistor [tolerance=±5% resistance=220 package=THT]
  R21 = Resistor [tolerance=±5% resistance=220 package=THT]
  R22 = Resistor [tolerance=±5% resistance=220 package=THT]
  R23 = Resistor [tolerance=±5% resistance=220 package=THT]
  R24 = Resistor [tolerance=±5% resistance=220 package=THT]
  R25 = Resistor [tolerance=±5% resistance=220 package=THT]
  Q30 = pnp-Powertransistor [package="TO220 [THT]"]
  D122 = Zener Diode [part_number=1N4732A breakdown_voltage=3.6V package="300 mil [THT]"]
  D123 = Zener Diode [part_number=1N4732A breakdown_voltage=3.6V package="300 mil [THT]"]
  D124 = Zener Diode [part_number=1N4732A breakdown_voltage=3.6V package="300 mil [THT]"]
  D125 = Zener Diode [part_number=1N4732A breakdown_voltage=3.6V package="300 mil [THT]"]
  D126 = Zener Diode [part_number=1N4732A breakdown_voltage=3.6V package="300 mil [THT]"]
  D127 = Zener Diode [part_number=1N4732A breakdown_voltage=3.6V package="300 mil [THT]"]
  D128 = Zener Diode [part_number=1N4732A breakdown_voltage=3.6V package="300 mil [THT]"]
  D129 = Zener Diode [part_number=1N4732A breakdown_voltage=3.6V package="300 mil [THT]"]
  J31 = shrouded pin header, 8 pins [form="♂ (shrouded male)"]
  J26 = shrouded pin header, 8 pins [form="♂ (shrouded male)"]
  J39 = shrouded pin header, 8 pins [form="♂ (shrouded male)"]
  J40 = shrouded pin header, 8 pins [form="♂ (shrouded male)"]
  J41 = shrouded pin header, 8 pins [form="♂ (shrouded male)"]
  J42 = shrouded pin header, 8 pins [form="♂ (shrouded male)"]
  J43 = shrouded pin header, 8 pins [form="♂ (shrouded male)"]
  J44 = shrouded pin header, 8 pins [form="♂ (shrouded male)"]
  J45 = shrouded pin header, 8 pins [form="♂ (shrouded male)"]
  D250 = Zener Diode [part_number=1N4732A breakdown_voltage=3.6V package="300 mil [THT]"]
  D251 = Zener Diode [part_number=1N4732A breakdown_voltage=3.6V package="300 mil [THT]"]
  D252 = Zener Diode [part_number=1N4732A breakdown_voltage=3.6V package="300 mil [THT]"]
  D253 = Zener Diode [part_number=1N4732A breakdown_voltage=3.6V package="300 mil [THT]"]
  D254 = Zener Diode [part_number=1N4732A breakdown_voltage=3.6V package="300 mil [THT]"]
  D255 = Zener Diode [part_number=1N4732A breakdown_voltage=3.6V package="300 mil [THT]"]
  D256 = Zener Diode [part_number=1N4732A breakdown_voltage=3.6V package="300 mil [THT]"]
  D257 = Zener Diode [part_number=1N4732A breakdown_voltage=3.6V package="300 mil [THT]"]
  J55 = shrouded pin header, 8 pins [form="♂ (shrouded male)"]
  D258 = Zener Diode [part_number=1N4732A breakdown_voltage=3.6V package="300 mil [THT]"]
  D259 = Zener Diode [part_number=1N4732A breakdown_voltage=3.6V package="300 mil [THT]"]
  D260 = Zener Diode [part_number=1N4732A breakdown_voltage=3.6V package="300 mil [THT]"]
  D261 = Zener Diode [part_number=1N4732A breakdown_voltage=3.6V package="300 mil [THT]"]
  D262 = Zener Diode [part_number=1N4732A breakdown_voltage=3.6V package="300 mil [THT]"]
  D263 = Zener Diode [part_number=1N4732A breakdown_voltage=3.6V package="300 mil [THT]"]
  D264 = Zener Diode [part_number=1N4732A breakdown_voltage=3.6V package="300 mil [THT]"]
  D265 = Zener Diode [part_number=1N4732A breakdown_voltage=3.6V package="300 mil [THT]"]
  J56 = shrouded pin header, 8 pins [form="♂ (shrouded male)"]
  D266 = Zener Diode [part_number=1N4732A breakdown_voltage=3.6V package="300 mil [THT]"]
  D267 = Zener Diode [part_number=1N4732A breakdown_voltage=3.6V package="300 mil [THT]"]
  D268 = Zener Diode [part_number=1N4732A breakdown_voltage=3.6V package="300 mil [THT]"]
  D269 = Zener Diode [part_number=1N4732A breakdown_voltage=3.6V package="300 mil [THT]"]
  D270 = Zener Diode [part_number=1N4732A breakdown_voltage=3.6V package="300 mil [THT]"]
  D271 = Zener Diode [part_number=1N4732A breakdown_voltage=3.6V package="300 mil [THT]"]
  D272 = Zener Diode [part_number=1N4732A breakdown_voltage=3.6V package="300 mil [THT]"]
  D273 = Zener Diode [part_number=1N4732A breakdown_voltage=3.6V package="300 mil [THT]"]
  J57 = shrouded pin header, 8 pins [form="♂ (shrouded male)"]
  D274 = Zener Diode [part_number=1N4732A breakdown_voltage=3.6V package="300 mil [THT]"]
  D275 = Zener Diode [part_number=1N4732A breakdown_voltage=3.6V package="300 mil [THT]"]
  D276 = Zener Diode [part_number=1N4732A breakdown_voltage=3.6V package="300 mil [THT]"]
  D277 = Zener Diode [part_number=1N4732A breakdown_voltage=3.6V package="300 mil [THT]"]
  D278 = Zener Diode [part_number=1N4732A breakdown_voltage=3.6V package="300 mil [THT]"]
  D279 = Zener Diode [part_number=1N4732A breakdown_voltage=3.6V package="300 mil [THT]"]
  D280 = Zener Diode [part_number=1N4732A breakdown_voltage=3.6V package="300 mil [THT]"]
  D281 = Zener Diode [part_number=1N4732A breakdown_voltage=3.6V package="300 mil [THT]"]
  J58 = shrouded pin header, 8 pins [form="♂ (shrouded male)"]
  D282 = Zener Diode [part_number=1N4732A breakdown_voltage=3.6V package="300 mil [THT]"]
  D283 = Zener Diode [part_number=1N4732A breakdown_voltage=3.6V package="300 mil [THT]"]
  D284 = Zener Diode [part_number=1N4732A breakdown_voltage=3.6V package="300 mil [THT]"]
  D285 = Zener Diode [part_number=1N4732A breakdown_voltage=3.6V package="300 mil [THT]"]
  D286 = Zener Diode [part_number=1N4732A breakdown_voltage=3.6V package="300 mil [THT]"]
  D287 = Zener Diode [part_number=1N4732A breakdown_voltage=3.6V package="300 mil [THT]"]
  D288 = Zener Diode [part_number=1N4732A breakdown_voltage=3.6V package="300 mil [THT]"]
  D289 = Zener Diode [part_number=1N4732A breakdown_voltage=3.6V package="300 mil [THT]"]
  J59 = shrouded pin header, 8 pins [form="♂ (shrouded male)"]
  D290 = Zener Diode [part_number=1N4732A breakdown_voltage=3.6V package="300 mil [THT]"]
  D291 = Zener Diode [part_number=1N4732A breakdown_voltage=3.6V package="300 mil [THT]"]
  D292 = Zener Diode [part_number=1N4732A breakdown_voltage=3.6V package="300 mil [THT]"]
  D293 = Zener Diode [part_number=1N4732A breakdown_voltage=3.6V package="300 mil [THT]"]
  D294 = Zener Diode [part_number=1N4732A breakdown_voltage=3.6V package="300 mil [THT]"]
  D295 = Zener Diode [part_number=1N4732A breakdown_voltage=3.6V package="300 mil [THT]"]
  D296 = Zener Diode [part_number=1N4732A breakdown_voltage=3.6V package="300 mil [THT]"]
  D297 = Zener Diode [part_number=1N4732A breakdown_voltage=3.6V package="300 mil [THT]"]
  J60 = shrouded pin header, 8 pins [form="♂ (shrouded male)"]
  D298 = Zener Diode [part_number=1N4732A breakdown_voltage=3.6V package="300 mil [THT]"]
  D299 = Zener Diode [part_number=1N4732A breakdown_voltage=3.6V package="300 mil [THT]"]
  D300 = Zener Diode [part_number=1N4732A breakdown_voltage=3.6V package="300 mil [THT]"]
  D301 = Zener Diode [part_number=1N4732A breakdown_voltage=3.6V package="300 mil [THT]"]
  D302 = Zener Diode [part_number=1N4732A breakdown_voltage=3.6V package="300 mil [THT]"]
  D303 = Zener Diode [part_number=1N4732A breakdown_voltage=3.6V package="300 mil [THT]"]
  D304 = Zener Diode [part_number=1N4732A breakdown_voltage=3.6V package="300 mil [THT]"]
  D305 = Zener Diode [part_number=1N4732A breakdown_voltage=3.6V package="300 mil [THT]"]
  J61 = shrouded pin header, 8 pins [form="♂ (shrouded male)"]

nets:
  N1: Part1.A2, Q27.base, R21.Pin_0
  N2: Part1.A3, Q26.base, R17.Pin_0
  N3: Part1.A4/SDA, Q25.base, R24.Pin_0
  N4: Part1.A5/SCL, Q24.base, R25.Pin_0
  N5: Part1.D8, R11.Pin_0
  N6: Part1.D9_PWM, R9.Pin_0
  N7: Part1.D10_PWM/SS, R7.Pin_0
  N8: Part1.D11_PWM/MOSI, R5.Pin_0
  N9: Part1.D12/MISO, R3.Pin_0
  N10: Part1.D13/SCK, R2.Pin_0
  GND: Part1.GND, Q9.E, Power_plug4.GND, Q11.E, Q13.E, Q15.E, Q17.E, Q19.E, Q21.E, Q23.E, Q24.emitter, Q25.emitter, Q26.emitter, Q27.emitter, Q28.emitter, Q29.emitter, Q31.emitter, R17.Pin_1, R18.Pin_1, R19.Pin_1, R21.Pin_1, R22.Pin_1, R23.Pin_1, R24.Pin_1, R25.Pin_1, Q30.emitter
  N11: Part1.D2, Q28.base, R22.Pin_0
  N12: Part1.D3_PWM, Q29.base, R23.Pin_0
  N13: Part1.D4, R19.Pin_0, Q30.base
  N14: Part1.D5_PWM, Q31.base, R18.Pin_0
  N15: Part1.D6_PWM, R15.Pin_0
  N16: Part1.D7, R13.Pin_0
  N17: R1.Pin_0, Q8.emitter, Power_plug4.VCC, R4.Pin_0, Q10.emitter, R6.Pin_0, Q12.emitter, R8.Pin_0, Q14.emitter, R10.Pin_0, Q16.emitter, R12.Pin_0, Q18.emitter, R14.Pin_0, Q20.emitter, R16.Pin_0, Q22.emitter
  N18: R1.Pin_1, Q8.base, Q9.B
  N19: Q8.collector, D122.anode, D123.anode, D124.anode, D125.anode, D127.anode, D129.anode
  N20: Q9.C, R2.Pin_1
  N21: R3.Pin_1, Q11.C
  N22: R4.Pin_1, Q10.base, Q11.B
  N23: Q10.collector, D250.anode, D251.anode, D252.anode, D254.anode, D255.anode, D257.anode
  N24: R5.Pin_1, Q13.C
  N25: R6.Pin_1, Q12.base, Q13.B
  N26: Q12.collector, D258.anode, D259.anode, D260.anode, D262.anode, D263.anode, D265.anode
  N27: R7.Pin_1, Q15.C
  N28: R8.Pin_1, Q14.base, Q15.B
  N29: Q14.collector, D266.anode, D267.anode, D268.anode, D270.anode, D271.anode, D273.anode
  N30: R9.Pin_1, Q17.C
  N31: R10.Pin_1, Q16.base, Q17.B
  N32: Q16.collector, D282.anode, D283.anode, D284.anode, D286.anode, D287.anode, D289.anode
  N33: R11.Pin_1, Q19.C
  N34: R12.Pin_1, Q18.base, Q19.B
  N35: Q18.collector, D274.anode, D275.anode, D276.anode, D278.anode, D279.anode, D281.anode
  N36: R13.Pin_1, Q21.C
  N37: R14.Pin_1, Q20.base, Q21.B
  N38: Q20.collector, D298.anode, D299.anode, D300.anode, D302.anode, D303.anode, D305.anode
  N39: R15.Pin_1, Q23.C
  N40: R16.Pin_1, Q22.base, Q23.B
  N41: Q22.collector, D290.anode, D291.anode, D292.anode, D294.anode, D295.anode, D297.anode
  N42: Q24.collector, J26.pin1, J26.pin2, J26.pin3, J26.pin4, J26.pin5, J26.pin6, J26.pin7, J26.pin8
  N43: Q25.collector, J39.pin1, J39.pin2, J39.pin3, J39.pin4, J39.pin5, J39.pin6, J39.pin7, J39.pin8
  N44: Q26.collector, J40.pin1, J40.pin2, J40.pin3, J40.pin4, J40.pin5, J40.pin6, J40.pin7, J40.pin8
  N45: Q27.collector, J41.pin1, J41.pin2, J41.pin3, J41.pin4, J41.pin5, J41.pin6, J41.pin7, J41.pin8
  N46: Q28.collector, J45.pin1, J45.pin2, J45.pin3, J45.pin4, J45.pin5, J45.pin6, J45.pin7, J45.pin8
  N47: Q29.collector, J44.pin1, J44.pin2, J44.pin3, J44.pin4, J44.pin5, J44.pin6, J44.pin7, J44.pin8
  N48: Q31.collector, J42.pin1, J42.pin2, J42.pin3, J42.pin4, J42.pin5, J42.pin6, J42.pin7, J42.pin8
  N49: Q30.collector, J43.pin1, J43.pin2, J43.pin3, J43.pin4, J43.pin5, J43.pin6, J43.pin7, J43.pin8
  N50: D122.cathode, J31.pin3
  N51: D123.cathode, J31.pin2
  N52: D124.cathode, J31.pin1
  N53: D125.cathode, J31.pin8
  N54: D126.cathode, J31.pin7
  N55: D126.anode, D128.anode
  N56: D127.cathode, J31.pin5
  N57: D128.cathode, J31.pin6
  N58: D129.cathode, J31.pin4
  N59: D250.cathode, J55.pin2
  N60: D251.cathode, J55.pin4
  N61: D252.cathode, J55.pin1
  N62: D253.cathode, J55.pin7
  N63: D253.anode, D256.anode
  N64: D254.cathode, J55.pin5
  N65: D255.cathode, J55.pin8
  N66: D256.cathode, J55.pin6
  N67: D257.cathode, J55.pin3
  N68: D258.cathode, J56.pin2
  N69: D259.cathode, J56.pin4
  N70: D260.cathode, J56.pin1
  N71: D261.cathode, J56.pin7
  N72: D261.anode, D264.anode
  N73: D262.cathode, J56.pin5
  N74: D263.cathode, J56.pin8
  N75: D264.cathode, J56.pin6
  N76: D265.cathode, J56.pin3
  N77: D266.cathode, J57.pin2
  N78: D267.cathode, J57.pin4
  N79: D268.cathode, J57.pin1
  N80: D269.cathode, J57.pin7
  N81: D269.anode, D272.anode
  N82: D270.cathode, J57.pin5
  N83: D271.cathode, J57.pin8
  N84: D272.cathode, J57.pin6
  N85: D273.cathode, J57.pin3
  N86: D274.cathode, J58.pin2
  N87: D275.cathode, J58.pin4
  N88: D276.cathode, J58.pin1
  N89: D277.cathode, J58.pin7
  N90: D277.anode, D280.anode
  N91: D278.cathode, J58.pin5
  N92: D279.cathode, J58.pin8
  N93: D280.cathode, J58.pin6
  N94: D281.cathode, J58.pin3
  N95: D282.cathode, J59.pin2
  N96: D283.cathode, J59.pin4
  N97: D284.cathode, J59.pin1
  N98: D285.cathode, J59.pin7
  N99: D285.anode, D288.anode
  N100: D286.cathode, J59.pin5
  N101: D287.cathode, J59.pin8
  N102: D288.cathode, J59.pin6
  N103: D289.cathode, J59.pin3
  N104: D290.cathode, J60.pin2
  N105: D291.cathode, J60.pin4
  N106: D292.cathode, J60.pin1
  N107: D293.cathode, J60.pin7
  N108: D293.anode, D296.anode
  N109: D294.cathode, J60.pin5
  N110: D295.cathode, J60.pin8
  N111: D296.cathode, J60.pin6
  N112: D297.cathode, J60.pin3
  N113: D298.cathode, J61.pin2
  N114: D299.cathode, J61.pin4
  N115: D300.cathode, J61.pin1
  N116: D301.cathode, J61.pin7
  N117: D301.anode, D304.anode
  N118: D302.cathode, J61.pin5
  N119: D303.cathode, J61.pin8
  N120: D304.cathode, J61.pin6
  N121: D305.cathode, J61.pin3
