# Fritzing sketch arduinobb (saved by Fritzing 0.9.1b)
circuit board: 5.97568cm x 3.48716cm
stripboards: 1

parts:
  J10 = female pin header, 6 pins [form="♀ (female rounded)"]
  J10_2 = female pin header, 4 pins [form="♀ (female rounded)"]
  J12 = female pin header, 5 pins [form="♀ (female rounded)"]
  J13 = female pin header, 6 pins [form="♀ (female rounded)"]
  ICSP = female pin header, 6 pins [form="♀ (female rounded)"]
  U6 = atmega168 [package=dip]
  C10 = Electrolytic Capacitor [capacitance=1µF package="200 mil [THT, electrolytic]"]
  C10_2 = Electrolytic Capacitor [capacitance=47µF package="200 mil [THT, electrolytic]"]
  S4 = Pushbutton [package="[THT]"]
  U5 = Voltage Regulator - 5V [package="TO220 [THT]"]
  XTAL3 = Crystal [frequency="16 Mhz" package=THT]
  C11 = Ceramic Capacitor [capacitance=22pF voltage=6.3V package="200 mil [THT, multilayer]"]
  C12 = Ceramic Capacitor [capacitance=100nF package="100 mil [THT, multilayer]"]
  J14 = Screw terminal - 2 pins [package=THT]
  C10_3 = Ceramic Capacitor [capacitance=22pF package="200 mil [THT, multilayer]"]
  D3 = Rectifier Diode [part_number=1N4001 package="300 mil [THT]"]
  D3_2 = Rectifier Diode [part_number=1N4001 package="300 mil [THT]"]
  R4 = Resistor [tolerance=±5% resistance=1k package=THT]

nets:
  N1: J10.pin1, U6.RESET, S4.Pin_1, S4.Pin_2, C12.1, R4.Pin_0
  N2: J10.pin2, ICSP.pin3, U6.D0_(RX)
  N3: J10.pin3, ICSP.pin2, U6.D1_(TX)
  N4: J10.pin4, U6.D2
  N5: J10.pin5, U6.D3_(PWM)
  N6: J10.pin6, U6.D4
  N7: J10_2.pin1, U6.D5_(PWM)
  N8: J10_2.pin2, U6.D6_(PWM)
  N9: J10_2.pin3, U6.D7
  N10: J10_2.pin4, U6.D8
  N11: J12.pin1, U6.D13
  N12: J12.pin2, U6.D12
  N13: J12.pin3, U6.D11_(PWM)
  N14: J12.pin4, U6.D10_(PWM)
  N15: J12.pin5, U6.D9_(PWM)
  N16: J13.pin1, U6.A5
  N17: J13.pin2, U6.A4
  N18: J13.pin3, U6.A3
  N19: J13.pin4, U6.A2
  N20: J13.pin5, U6.A1
  N21: J13.pin6, U6.A0
  N22: ICSP.pin1, C12.0
  N23: ICSP.pin4, U6.VCC, U6.AVCC, U6.AREF, C10.+, U5.output_voltage, R4.Pin_1
  GND: ICSP.pin5, ICSP.pin6, U6.GND, C10.-, C10_2.-, S4.Pin_3, S4.Pin_4, U5.GND, C11.1, J14.pin2, C10_3.0
  N24: U6.XLAT1, XTAL3.pin_0, C10_3.1
  N25: U6.XLAT2, XTAL3.pin_1, C11.0
  N26: C10_2.+, U5.input_voltage, D3.cathode, D3_2.cathode
  N27: J14.pin1, D3.anode, D3_2.anode

notes:
  This is a stripboard Arduino without an FTDI chip. You can load sketches on the chip through the FTDI header (like the Lily Pad).
  http://arduino.cc/en/Guide/ArduinoLilyPad
