# Fritzing sketch vga (saved by Fritzing 0.9.1b)
circuit board: 14.5767cm x 14.7507cm
breadboards: 1

parts:
  Part1 = Arduino Mega ADK (Rev3)
  ZIF_SOCKET1 = Aries 28-6574-10 28W ZIF Socket [part_number=28-6574-10]
  Q1 = PNP-Transistor [package="TO92 [THT]"]
  R1 = Resistor [tolerance=±5% resistance=220 package=THT]
  R2 = Resistor [tolerance=±5% resistance=220 package=THT]
  R4 = Resistor [tolerance=±5% resistance=220 package=THT]
  R3 = Resistor [tolerance=±5% resistance=220 package=THT]
  J5 = Screw terminal - 2 pins [package=THT]
  LED1 = LED - 5mm [color="Red (633nm)" package="5 mm [THT]"]
  R5 = Trimmer Potentiometer [maximum_resistance=10kΩ package=THT]
  J2 = Screw terminal - 2 pins [package=THT]
  J4 = screw terminal, 2 pins
  J3 = Screw terminal - 2 pins [package=THT]

nets:
  N1: Part1.GND, ZIF_SOCKET1.Pin_14, ZIF_SOCKET1.Pin_20, ZIF_SOCKET1.Pin_22, Q1.E, J5.pin2, LED1.cathode, J2.pin1
  N2: Part1.D13_PWM, Q1.B
  N3: Part1.D11_PWM, R3.Pin_1
  N4: Part1.D9_PWM, ZIF_SOCKET1.Pin_19
  N5: Part1.D8_PWM, ZIF_SOCKET1.Pin_18
  N6: Part1.IOREF, Part1.5V, ZIF_SOCKET1.Pin_1, ZIF_SOCKET1.Pin_28, R5.leg1
  N7: Part1.VIN, J5.pin1
  N8: Part1.D2_PWM, ZIF_SOCKET1.Pin_11
  N9: Part1.D3_PWM, ZIF_SOCKET1.Pin_12
  N10: Part1.D4_PWM, ZIF_SOCKET1.Pin_13
  N11: Part1.D5_PWM, ZIF_SOCKET1.Pin_15
  N12: Part1.D6_PWM, ZIF_SOCKET1.Pin_16
  N13: Part1.D7_PWM, ZIF_SOCKET1.Pin_17
  N14: Part1.D23, R2.Pin_1
  N15: Part1.D29, R4.Pin_1
  N16: Part1.D30, ZIF_SOCKET1.Pin_10
  N17: Part1.D31, ZIF_SOCKET1.Pin_9
  N18: Part1.D32, ZIF_SOCKET1.Pin_8
  N19: Part1.D33, ZIF_SOCKET1.Pin_7
  N20: Part1.D34, ZIF_SOCKET1.Pin_6
  N21: Part1.D35, ZIF_SOCKET1.Pin_5
  N22: Part1.D36, ZIF_SOCKET1.Pin_4
  N23: Part1.D37, ZIF_SOCKET1.Pin_3
  N24: Part1.D38, ZIF_SOCKET1.Pin_25
  N25: Part1.D39, ZIF_SOCKET1.Pin_24
  N26: Part1.D40, ZIF_SOCKET1.Pin_21
  N27: Part1.D41, ZIF_SOCKET1.Pin_23
  N28: Part1.D42, ZIF_SOCKET1.Pin_2
  N29: Part1.D43, R1.Pin_1
  N30: Part1.D44, ZIF_SOCKET1.Pin_26
  N31: Part1.D45, ZIF_SOCKET1.Pin_27
  N32: R1.Pin_0, J4.pin2
  N33: R2.Pin_0, J4.pin1
  N34: R4.Pin_0, J3.pin2
  N35: R3.Pin_0, J3.pin1
  N36: LED1.anode, R5.wiper
